# Fritzing sketch battleremote-mark2 (saved by Fritzing 0.9.4)
breadboards: 1

parts:
  Part1 = Arduino Nano (Rev3.0)
  VCC1 = Battery block 9V
  Part2 = Bluetooth HC-05 Macho  # not connected
  Grove1 = Grove OLED 128x96
  U2 = JOYSTICK-PSP1000 [package=joystick-psp1000]
  R1 = Resistor [tolerance=±5% resistance=1k package=THT]
  R2 = Resistor [tolerance=±5% resistance=2.0k package=THT]

nets:
  GND: Part1.GND, VCC1.-, Grove1.GND, U2.GND, R2.Pin_0
  N1: Part1.D3, R1.Pin_0
  N2: Part1.VIN, VCC1.+
  VCC: Part1.5V, Grove1.VCC, U2.VCC
  N3: Part1.A7, Part1.A6, U2.X, U2.Y
  N4: Part1.A5, Grove1.SCL
  N5: Part1.A4, Grove1.SDA
  N6: R1.Pin_1, R2.Pin_1

notes:
  VRX
  VRY
  +5V
  GND
  joystick
  OLED display
  9v battery
  arduino
  bluetooth
  1K resistor
  2K resistor
  battlebot remote
